# Fritzing sketch button_irq (saved by Fritzing 0.9.9b)
breadboards: 2

parts:
  Mod1 = Raspberry Pi Pico
  Mod2 = Raspberry Pi Pico
  S1 = Momentary Switch [package=ksa_sealed_tac_switch]
  R11 = Resistor [tolerance=±5% resistance=10k package="1206 [SMD]"]
  R12 = Resistor [tolerance=±5% resistance=10k package="1206 [SMD]"]

nets:
  UART0_TX: Mod1.pin_1, Mod2.pin_7
  UART0_RX: Mod1.pin_2, Mod2.pin_6
  GND: Mod1.pin_3, Mod1.pin_8, Mod1.pin_13, Mod1.pin_18, Mod1.pin_23, Mod1.pin_28, Mod1.pin_33, Mod1.pin_38, Mod1.pin_42, Mod2.pin_3, Mod2.pin_8, Mod2.pin_13, Mod2.pin_18, Mod2.pin_23, Mod2.pin_28, Mod2.pin_33, Mod2.pin_38, S1.2
  button: Mod1.pin_17, R11.Pin_0
  3.3V: Mod1.pin_36, R12.Pin_0
  5V: Mod1.pin_39, Mod2.pin_39
  SW_CLK: Mod1.pin_41, Mod2.pin_4
  SW_DIO: Mod1.pin_43, Mod2.pin_5
  N1: S1.3, R12.Pin_1
  N2: S1.4, R11.Pin_1

custom parts:
  Raspberry Pi Pico: Raspberry Pi Pico. Based around the RP2040 microcontroller the Pico is a low cost microcontroller device bringing Raspberry Pi quality, cost, and easy of use to the microcontroller space. Jan 2021, Split part in to two versions: tht (this one) and SMD. This one will drill holes for a .1 in header in pcb to allow plugging in the module as well as providing pads to solder the module to the top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
