# Fritzing sketch seven_segment_display (saved by Fritzing 0.9.9b)
breadboards: 2

parts:
  U1 = 74HC595 [package="DIP16 [THT]"]
  Mod1 = Raspberry Pi Pico
  R7 = Resistor [tolerance=±5% resistance=220 power=0.25 package=THT]
  R6 = Resistor [tolerance=±5% resistance=220 power=0.25 package=THT]
  R4 = Resistor [tolerance=±5% resistance=220 power=0.25 package=THT]
  R3 = Resistor [tolerance=±5% resistance=220 power=0.25 package=THT]
  R2 = Resistor [tolerance=±5% resistance=220 power=0.25 package=THT]
  R1 = Resistor [tolerance=±5% resistance=220 power=0.25 package=THT]
  Mod2 = Raspberry Pi Pico
  R9 = Resistor [tolerance=±5% resistance=220 power=0.25 package=THT]
  7_Segment_4_Digit_Display2 = 7-SEGMENT-4DIGIT common cathode [part_number=HS420561K-32 package=7-segment-4digit-cathode]
  R10 = Resistor [tolerance=±5% resistance=220 power=0.25 package=THT]
  S1 = Momentary Switch [package=ksa_sealed_tac_switch]
  R11 = Resistor [tolerance=±5% resistance=10k package="1206 [SMD]"]
  R12 = Resistor [tolerance=±5% resistance=10k package="1206 [SMD]"]

nets:
  G: U1.Q1, R4.Pin_0
  F: U1.Q2, R3.Pin_1
  E: U1.Q3, R10.Pin_0
  D: U1.Q4, R7.Pin_0
  C: U1.Q5, R6.Pin_1
  B: U1.Q6, R1.Pin_0
  A: U1.Q7, R2.Pin_1
  GND: U1.GND, U1.OE, Mod1.pin_3, Mod1.pin_8, Mod1.pin_13, Mod1.pin_18, Mod1.pin_23, Mod1.pin_28, Mod1.pin_33, Mod1.pin_38, Mod1.pin_42, Mod2.pin_3, Mod2.pin_8, Mod2.pin_13, Mod2.pin_18, Mod2.pin_23, Mod2.pin_28, Mod2.pin_33, Mod2.pin_38, S1.2
  5V: U1.MR, U1.VCC, Mod1.pin_39, Mod2.pin_39
  clock: U1.SH_CP, Mod1.pin_27
  latch: U1.ST_CP, Mod1.pin_26
  data: U1.DS, Mod1.pin_24
  DP: U1.Q0, R9.Pin_1
  UART0_TX: Mod1.pin_1, Mod2.pin_7
  UART0_RX: Mod1.pin_2, Mod2.pin_6
  button: Mod1.pin_17, R11.Pin_0
  D4: Mod1.pin_19, 7_Segment_4_Digit_Display2.pin_6
  D3: Mod1.pin_20, 7_Segment_4_Digit_Display2.pin_8
  D2: Mod1.pin_21, 7_Segment_4_Digit_Display2.pin_9
  D1: Mod1.pin_22, 7_Segment_4_Digit_Display2.pin_12
  3.3V: Mod1.pin_36, R12.Pin_0
  SW_CLK: Mod1.pin_41, Mod2.pin_4
  SW_DIO: Mod1.pin_43, Mod2.pin_5
  N1: R7.Pin_1, 7_Segment_4_Digit_Display2.pin_2
  N2: R6.Pin_0, 7_Segment_4_Digit_Display2.pin_4
  N3: R4.Pin_1, 7_Segment_4_Digit_Display2.pin_5
  N4: R3.Pin_0, 7_Segment_4_Digit_Display2.pin_10
  N5: R2.Pin_0, 7_Segment_4_Digit_Display2.pin_11
  N6: R1.Pin_1, 7_Segment_4_Digit_Display2.pin_7
  N7: R9.Pin_0, 7_Segment_4_Digit_Display2.pin_3
  N8: 7_Segment_4_Digit_Display2.pin_1, R10.Pin_1
  N9: S1.3, R12.Pin_1
  N10: S1.4, R11.Pin_1

custom parts:
  Raspberry Pi Pico: Raspberry Pi Pico. Based around the RP2040 microcontroller the Pico is a low cost microcontroller device bringing Raspberry Pi quality, cost, and easy of use to the microcontroller space. Jan 2021, Split part in to two versions: tht (this one) and SMD. This one will drill holes for a .1 in header in pcb to allow plugging in the module as well as providing pads to solder the module to the top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
  7-SEGMENT-4DIGIT common cathode: A 7 Segment 4 Digit common cathode display, with decimal points
