# Fritzing sketch i2c_lcd (saved by Fritzing 0.9.9b)
breadboards: 2

parts:
  Mod1 = Raspberry Pi Pico
  Mod2 = Raspberry Pi Pico
  U1 = PCF8574 [package="DIP16 [THT]"]
  R1 = Resistor [tolerance=±5% power=0.25 resistance=10k package=THT]
  R2 = Trimmer Potentiometer [maximum_resistance=10kΩ package=THT]
  U2 = LCD-16X2 [package=lcd-16x2]
  R3 = Resistor [tolerance=±5% power=0.25 resistance=4.7k package=THT]
  R4 = Resistor [tolerance=±5% power=0.25 resistance=4.7k package=THT]
  R5 = Resistor [tolerance=±5% power=0.25 resistance=10k package=THT]
  R6 = Resistor [tolerance=±5% power=0.25 resistance=10k package=THT]
  R7 = Resistor [tolerance=±5% power=0.25 resistance=4.7k package=THT]
  Q1 = TRANSISTOR_NPN [part_number=8050 package=to-92]
  C2 = Capacitor [part_number=0.1uF package=cap-pth-small2]
  R8 = Trimmer Potentiometer [maximum_resistance=10kΩ package=THT]

nets:
  UART0_TX: Mod1.pin_1, Mod2.pin_7
  UART0_RX: Mod1.pin_2, Mod2.pin_6
  GND: Mod1.pin_3, Mod1.pin_8, Mod1.pin_13, Mod1.pin_18, Mod1.pin_23, Mod1.pin_28, Mod1.pin_33, Mod1.pin_38, Mod1.pin_42, Mod2.pin_3, Mod2.pin_8, Mod2.pin_13, Mod2.pin_18, Mod2.pin_23, Mod2.pin_28, Mod2.pin_33, Mod2.pin_38, U1.GND, R2.leg1, U2.VSS, Q1.E, C2.2, R8.leg2
  SDA: Mod1.pin_9, U1.SDA, R3.Pin_0
  SCL: Mod1.pin_10, U1.SCL, R4.Pin_0
  pot: Mod1.pin_31, R8.wiper
  3.3V: Mod1.pin_36, R8.leg1
  5V: Mod1.pin_39, Mod2.pin_39, U1.VCC, R1.Pin_0, R2.leg2, U2.VDD, R3.Pin_1, R4.Pin_1, R5.Pin_0, R6.Pin_0, R7.Pin_1, C2.1
  SW_CLK: Mod1.pin_41, Mod2.pin_4
  SW_DIO: Mod1.pin_43, Mod2.pin_5
  N1: U1.A0, R1.Pin_1
  N2: U1.A1, R5.Pin_1
  N3: U1.A2, R6.Pin_1
  LCD_RS: U1.P0, U2.RS
  LCD_RW: U1.P1, U2.R_W
  LCD_E: U1.P2, U2.E
  P3: U1.P3, R7.Pin_0, Q1.B
  LCD_DB4: U1.P4, U2.DB4
  LCD_DB5: U1.P5, U2.DB5
  LCD_DB6: U1.P6, U2.DB6
  LCD_DB7: U1.P7, U2.DB7
  LCD_VO: R2.wiper, U2.VO
  LCD_LED_P: U2.K, Q1.C

custom parts:
  Raspberry Pi Pico: Raspberry Pi Pico. Based around the RP2040 microcontroller the Pico is a low cost microcontroller device bringing Raspberry Pi quality, cost, and easy of use to the microcontroller space. Jan 2021, Split part in to two versions: tht (this one) and SMD. This one will drill holes for a .1 in header in pcb to allow plugging in the module as well as providing pads to solder the module to the top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
