# Fritzing sketch seven_segment_display (saved by Fritzing 0.9.9b)
breadboards: 2

parts:
  DI1 = 7-Segment LED Display [package=THT]
  U1 = 74HC595 [package="DIP16 [THT]"]
  Mod1 = Raspberry Pi Pico
  R8 = Resistor [tolerance=±5% resistance=220 power=0.25 package=THT]
  R7 = Resistor [tolerance=±5% resistance=220 power=0.25 package=THT]
  R6 = Resistor [tolerance=±5% resistance=220 power=0.25 package=THT]
  R5 = Resistor [tolerance=±5% resistance=220 power=0.25 package=THT]
  R4 = Resistor [tolerance=±5% resistance=220 power=0.25 package=THT]
  R3 = Resistor [tolerance=±5% resistance=220 power=0.25 package=THT]
  R2 = Resistor [tolerance=±5% resistance=220 power=0.25 package=THT]
  R1 = Resistor [tolerance=±5% resistance=220 power=0.25 package=THT]
  Mod2 = Raspberry Pi Pico

nets:
  N1: DI1.cathodeE, R8.Pin_1
  N2: DI1.cathodeD, R7.Pin_1
  5V: DI1.commAnode#2, U1.MR, U1.VCC, Mod1.pin_39, Mod2.pin_39
  N3: DI1.cathodeC, R6.Pin_0
  N4: DI1.cathodeDP, R5.Pin_0
  N5: DI1.cathodeB, R1.Pin_0
  N6: DI1.cathodeA, R2.Pin_0
  N7: DI1.cathodeF, R3.Pin_1
  N8: DI1.cathodeG, R4.Pin_1
  G: U1.Q1, R4.Pin_0
  F: U1.Q2, R3.Pin_0
  E: U1.Q3, R8.Pin_0
  D: U1.Q4, R7.Pin_0
  C: U1.Q5, R6.Pin_1
  B: U1.Q6, R1.Pin_1
  A: U1.Q7, R2.Pin_1
  GND: U1.GND, U1.OE, Mod1.pin_3, Mod1.pin_8, Mod1.pin_13, Mod1.pin_18, Mod1.pin_23, Mod1.pin_28, Mod1.pin_33, Mod1.pin_38, Mod1.pin_42, Mod2.pin_3, Mod2.pin_8, Mod2.pin_13, Mod2.pin_18, Mod2.pin_23, Mod2.pin_28, Mod2.pin_33, Mod2.pin_38
  clock: U1.SH_CP, Mod1.pin_27
  latch: U1.ST_CP, Mod1.pin_26
  data: U1.DS, Mod1.pin_24
  DP: U1.Q0, R5.Pin_1
  UART0_TX: Mod1.pin_1, Mod2.pin_7
  UART0_RX: Mod1.pin_2, Mod2.pin_6
  SW_CLK: Mod1.pin_41, Mod2.pin_4
  SW_DIO: Mod1.pin_43, Mod2.pin_5

custom parts:
  Raspberry Pi Pico: Raspberry Pi Pico. Based around the RP2040 microcontroller the Pico is a low cost microcontroller device bringing Raspberry Pi quality, cost, and easy of use to the microcontroller space. Jan 2021, Split part in to two versions: tht (this one) and SMD. This one will drill holes for a .1 in header in pcb to allow plugging in the module as well as providing pads to solder the module to the top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
